# Fritzing sketch wiring (saved by Fritzing 0.9.2b)
breadboards: 1

parts:
  WeMos_D1_Mini1 = WeMos D1 Mini
  Power_plug1 = Power plug
  Power_plug2 = Power plug
  KY-1 = Keyes Relay [package=THT]
  RGB_Strip_LED3 = RGB Strip LED
  Q3 = Basic FET N-Channel [package="DPak [SMD]"]
  Q4 = Basic FET N-Channel [package="DPak [SMD]"]
  Q5 = Basic FET N-Channel [package="DPak [SMD]"]
  J1 = Basic Servo

nets:
  VCC: WeMos_D1_Mini1.5V, Power_plug2.VCC, KY-1.power, J1.vcc
  N1: WeMos_D1_Mini1.D1, Q3.Gate
  N2: WeMos_D1_Mini1.D2, Q4.Gate
  N3: WeMos_D1_Mini1.D3, Q5.Gate
  N4: WeMos_D1_Mini1.D7, J1.pulse
  N5: WeMos_D1_Mini1.D8, KY-1.signal
  GND: WeMos_D1_Mini1.G, Power_plug2.GND, KY-1.ground, J1.gnd
  N6: Power_plug1.GND, Q3.source, Q4.source, Q5.source
  N7: Power_plug1.VCC, RGB_Strip_LED3.Common_Connect
  N8: KY-1.NC, KY-1.C, KY-1.NO
  N9: RGB_Strip_LED3.Green_Connect, Q4.drain
  N10: RGB_Strip_LED3.Red_Connect, Q3.drain
  N11: RGB_Strip_LED3.Blue_Connect, Q5.drain

notes:
  12V
  Led Strip Power
  5V
  Fish Feeder
  to 220VAC PUMP
  LAMP
  RGB Led Strip

custom parts:
  WeMos D1 Mini: The D1 mini is a mini wifi board based on ESP-8266EX.
  Keyes Relay: The Keyes 5V relay module is suitable for SCM development, home appliance control. It uses a 5V~12V TIL control signal which can control DC / AC signal.
  RGB Strip LED: A tri-color Strip LED with red, green and blue. Based on LED SMD 5050 RGB Pin order: common cathode - green - red - blue
